// Logisim project Diferença.circ as structural Verilog: 4 circuits, main circuit main
module main (
  input  Alet_4,
  input  Alet_3,
  input  Alet_2,
  input  Alet_1,
  input  Bit_4,
  input  Bit3,
  input  Bit2,
  input  Bit1,
  output Dif_5,
  output Dif_4,
  output Dif_3,
  output Dif_2,
  output Dif_1
);

  wire complementode2_1_ou1, complementode2_1_ou2, complementode2_1_ou3, complementode2_1_ou4;

  Complementode2 complementode2_1 (
    .Iu1(Bit1), .Iu2(Bit2), .Iu3(Bit3), .Iu4(Bit_4), .Ou1(complementode2_1_ou1), .Ou2(complementode2_1_ou2),
    .Ou3(complementode2_1_ou3), .Ou4(complementode2_1_ou4));
  Somador4bits somador4bits_1 (
    .A4(Alet_4), .A3(Alet_3), .A2(Alet_2), .A1(Alet_1), .I4(complementode2_1_ou4), .I3(complementode2_1_ou3),
    .I2(complementode2_1_ou2), .I1(complementode2_1_ou1), .Sf5(Dif_5), .Sf4(Dif_4), .Sf3(Dif_3), .Sf2(Dif_2),
    .Sf1(Dif_1));
endmodule

module Somador1bit (
  input  Cin,
  input  B,
  input  A,
  output S,
  output Cout
);

  wire and_1_out, and_2_out, and_3_out, xor_1_out;

  xor xor_1 (xor_1_out, A, B);
  and and_1 (and_1_out, B, A);
  and and_2 (and_2_out, A, Cin);
  and and_3 (and_3_out, Cin, B);
  or or_1 (Cout, and_1_out, and_2_out, and_3_out);
  xor xor_2 (S, xor_1_out, Cin);
endmodule

module Somador4bits (
  input  A4,
  input  A3,
  input  A2,
  input  A1,
  input  I4,
  input  I3,
  input  I2,
  input  I1,
  output Sf5,
  output Sf4,
  output Sf3,
  output Sf2,
  output Sf1
);

  wire somador1bit_2_cout, somador1bit_3_cout, somador1bit_4_cout;

  Somador1bit somador1bit_1 (.Cin(somador1bit_2_cout), .B(I4), .A(A4), .S(Sf4), .Cout(Sf5));
  Somador1bit somador1bit_2 (.Cin(somador1bit_3_cout), .B(I3), .A(A3), .S(Sf3), .Cout(somador1bit_2_cout));
  Somador1bit somador1bit_3 (.Cin(somador1bit_4_cout), .B(I2), .A(A2), .S(Sf2), .Cout(somador1bit_3_cout));
  Somador1bit somador1bit_4 (.Cin(1'b0), .B(I1), .A(A1), .S(Sf1), .Cout(somador1bit_4_cout));
endmodule

module Complementode2 (
  input  Iu1,
  input  Iu2,
  input  Iu3,
  input  Iu4,
  output Ou1,
  output Ou2,
  output Ou3,
  output Ou4
);

  wire not_1_out, not_2_out, not_3_out, not_4_out;

  not not_1 (not_1_out, Iu1);
  not not_2 (not_2_out, Iu2);
  not not_3 (not_3_out, Iu3);
  not not_4 (not_4_out, Iu4);
  Somador1bit somador1bit_1 (.Cin(1'b0), .B(not_1_out), .A(1'b1), .S(Ou1));  // open: Cout
  Somador1bit somador1bit_2 (.Cin(1'b0), .B(not_2_out), .A(1'b1), .S(Ou2));  // open: Cout
  Somador1bit somador1bit_3 (.Cin(1'b0), .B(not_3_out), .A(1'b1), .S(Ou3));  // open: Cout
  Somador1bit somador1bit_4 (.Cin(1'b0), .B(not_4_out), .A(1'b1), .S(Ou4));  // open: Cout
endmodule
